# Fritzing sketch sketch (saved by Fritzing 0.9.3b)

parts:
  M1 = DC Motor
  M2 = DC Motor
  VCC1 = 4 x AAA Battery Mount
  VCC2 = Battery
  L298N2 = L298N DC motor driver
  M3 = RioRand LM2596
  J1 = Camdenboss CTB0158-8 [part_number=CTB0158-8 package=THT]
  J2 = Camdenboss CTB0158-6 [part_number=CTB0158-6 package=THT]  # not connected
  J3 = Camdenboss CTB0158-8 [part_number=CTB0158-8 package=THT]
  J4 = Camdenboss CTB0158-10 [part_number=CTB0158-10 package=THT]
  J5 = Power Jack [package=power_jack_smd]
  Part1 = NRF24L01+ Breakout Board

nets:
  N1: M1.pin_1, L298N2.OUT4
  N2: M1.pin_2, L298N2.OUT3
  N3: M2.pin_1, L298N2.OUT2
  N4: M2.pin_2, L298N2.OUT1
  N5: VCC1.+, L298N2.12V, M3.Pin_1
  N6: VCC2.-, L298N2.GND, M3.Pin_2
  N7: L298N2.ENA, J3.terminal_1
  N8: L298N2.ENB, J3.terminal_2
  N9: L298N2.IN1, J3.terminal_3
  N10: L298N2.IN2, J3.terminal_4
  N11: L298N2.IN3, J3.terminal_5
  N12: L298N2.IN4, J3.terminal_6
  N13: M3.Pin_3, J5.PWR
  N14: J1.terminal_4, Part1.VCC
  N15: J1.terminal_7, Part1.GND
  N16: J4.terminal_5, Part1.SCK
  N17: J4.terminal_6, Part1.MISO
  N18: J4.terminal_7, Part1.MOSI
  N19: J4.terminal_8, Part1.CS
  N20: J4.terminal_9, Part1.IRQ
  N21: J4.terminal_10, Part1.CE

custom parts:
  L298N DC motor driver: 2x DC motor driver with 78M05 positive voltage regulator (7..35 V) L298N: max 46 V, 2 A Set 5 V Enable jumper to enable 5 V regultor (needed for the L298N) and +5 V output at screw terminal or supply external +5 V at screw terminal Set ENA and/or ENB to +5 V to enable motor permanently or supply ENA and/or ENB with PWM signal IN1 and IN2 set rotation directory for motor A (OUT1/OUT2) IN2 and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
